# Fritzing sketch Codigo_03 (saved by Fritzing 0.9.3b)
breadboards: 1

parts:
  Componente1 = Arduino Uno (Rev3)
  R1 = Resistor [tolerance=±5% resistance=330 package=THT]
  LED1 = LED - 5mm [color="Red (633nm)" package="5 mm [THT]"]
  S1 = Pushbutton [package="[THT]"]
  S2 = Pushbutton [package="[THT]"]
  R2 = Resistor [tolerance=±5% resistance=1k package=THT]
  R3 = Resistor [tolerance=±5% resistance=1k package=THT]

nets:
  N1: Componente1.D13/SCK, LED1.anode
  N2: Componente1.GND, R1.Pin_0, R2.Pin_0, R3.Pin_0
  N3: Componente1.D2, S2.Pin_1, S2.Pin_2
  N4: Componente1.D3_PWM, S1.Pin_1, S1.Pin_2
  N5: R1.Pin_1, LED1.cathode
  N6: S1.Pin_3, S1.Pin_4, R2.Pin_1
  N7: S2.Pin_3, S2.Pin_4, R3.Pin_1

notes:
  CIRCUITO 03
