# Fritzing sketch Codigo_01 (saved by Fritzing 0.9.3b)
breadboards: 1

parts:
  Componente1 = Arduino Uno (Rev3)
  R1 = Resistor [tolerance=±5% resistance=330 package=THT]
  LED1 = LED - 5mm [color="Red (633nm)" package="5 mm [THT]"]

nets:
  N1: Componente1.D13/SCK, LED1.anode
  N2: Componente1.GND, R1.Pin_0
  N3: R1.Pin_1, LED1.cathode

notes:
  CIRCUITO 01
