# Fritzing sketch Codigo_02 (saved by Fritzing 0.9.3b)
breadboards: 1

parts:
  Componente1 = Arduino Uno (Rev3)
  R1 = Resistor [tolerance=±5% resistance=330 package=THT]
  LED1 = LED - 5mm [color="Red (633nm)" package="5 mm [THT]"]
  R2 = TRIMPOT [package=3362u-2]

nets:
  N1: Componente1.A0, R2.WIPER
  N2: Componente1.D13/SCK, LED1.anode
  N3: Componente1.5V, R2.CW
  N4: Componente1.GND, R1.Pin_0, R2.CCW
  N5: R1.Pin_1, LED1.cathode

notes:
  CIRCUITO 02
