# Fritzing sketch Codigo_04 (saved by Fritzing 0.9.3b)
breadboards: 1

parts:
  Componente1 = Arduino Uno (Rev3)
  R2 = Resistor [tolerance=±5% resistance=330 package=THT]
  LED2 = LED - 5mm [color="Blue (470nm)" package="5 mm [THT]"]
  R3 = Resistor [tolerance=±5% resistance=330 package=THT]
  LED3 = LED - 5mm [color="Yellow (585nm)" package="5 mm [THT]"]
  R4 = Resistor [tolerance=±5% resistance=330 package=THT]
  LED4 = LED - 5mm [color="Red (633nm)" package="5 mm [THT]"]
  R5 = Resistor [tolerance=±5% resistance=330 package=THT]
  LED5 = LED - 5mm [color="Yellow (585nm)" package="5 mm [THT]"]
  R6 = Resistor [tolerance=±5% resistance=330 package=THT]
  LED6 = LED - 5mm [color="Blue (470nm)" package="5 mm [THT]"]
  R7 = Resistor [tolerance=±5% resistance=330 package=THT]
  LED7 = LED - 5mm [color="Yellow (585nm)" package="5 mm [THT]"]
  R8 = Resistor [tolerance=±5% resistance=330 package=THT]
  LED8 = LED - 5mm [color="Red (633nm)" package="5 mm [THT]"]
  R9 = Resistor [tolerance=±5% resistance=330 package=THT]
  LED9 = LED - 5mm [color="Yellow (585nm)" package="5 mm [THT]"]

nets:
  N1: Componente1.D8, LED8.anode
  N2: Componente1.D9_PWM, LED9.anode
  N3: Componente1.D2, LED2.anode
  N4: Componente1.D3_PWM, LED3.anode
  N5: Componente1.D4, LED4.anode
  N6: Componente1.D5_PWM, LED5.anode
  N7: Componente1.D6_PWM, LED6.anode
  N8: Componente1.D7, LED7.anode
  N9: Componente1.GND, R2.Pin_0, R3.Pin_0, R4.Pin_0, R5.Pin_0, R6.Pin_0, R7.Pin_0, R8.Pin_0, R9.Pin_0
  N10: R2.Pin_1, LED2.cathode
  N11: R3.Pin_1, LED3.cathode
  N12: R4.Pin_1, LED4.cathode
  N13: R5.Pin_1, LED5.cathode
  N14: R6.Pin_1, LED6.cathode
  N15: R7.Pin_1, LED7.cathode
  N16: R8.Pin_1, LED8.cathode
  N17: R9.Pin_1, LED9.cathode

notes:
  CIRCUITO 04
