# Fritzing sketch Codigo_05 (saved by Fritzing 0.9.3b)
breadboards: 1

parts:
  Componente1 = Arduino Uno (Rev3)
  R2 = Resistor [tolerance=±5% resistance=330 package=THT]
  R3 = Resistor [tolerance=±5% resistance=330 package=THT]
  R4 = Resistor [tolerance=±5% resistance=330 package=THT]
  R10 = TRIMPOT [package=3362u-2]
  R11 = TRIMPOT [package=3362u-2]
  R12 = TRIMPOT [package=3362u-2]
  LED1 = RGB LED (com. cathode, rbg) [package="5 mm [THT]"]

nets:
  N1: Componente1.A0, R10.WIPER
  N2: Componente1.A1, R11.WIPER
  N3: Componente1.A2, R12.WIPER
  N4: Componente1.D9_PWM, R2.Pin_0
  N5: Componente1.D10_PWM/SS, R3.Pin_0
  N6: Componente1.D11_PWM/MOSI, R4.Pin_0
  N7: Componente1.5V, R10.CW, R11.CW, R12.CW
  N8: Componente1.GND, R10.CCW, R11.CCW, R12.CCW, LED1.common_cathode
  N9: R2.Pin_1, LED1.green_anode
  N10: R3.Pin_1, LED1.blue_anode
  N11: R4.Pin_1, LED1.red_anode

notes:
  CIRCUITO 05
