# Fritzing sketch Codigo_06 (saved by Fritzing 0.9.3b)
breadboards: 1

parts:
  Componente1 = Arduino Uno (Rev3)
  R4 = Resistor [tolerance=±5% resistance=330 package=THT]
  LED1 = LED - 5mm [color="Red (633nm)" package="5 mm [THT]"]
  R5 = Photocell (LDR) [package=THT]
  R6 = Resistor [tolerance=±5% resistance=1k package=THT]

nets:
  N1: Componente1.A0, R5.pin_1, R6.Pin_1
  N2: Componente1.D9_PWM, LED1.anode
  N3: Componente1.5V, R5.pin_0
  N4: Componente1.GND, R4.Pin_0, R6.Pin_0
  N5: R4.Pin_1, LED1.cathode

notes:
  CIRCUITO 06
