# Fritzing sketch Codigo_07 (saved by Fritzing 0.9.3b)
breadboards: 1

parts:
  Componente1 = Arduino Uno (Rev3)
  R6 = Resistor [tolerance=±5% resistance=10k package=THT]
  DHT1 = DHT22 Humidity and Temperature Sensor

nets:
  N1: Componente1.D2, R6.Pin_1, DHT1.DATA
  5V: Componente1.5V, R6.Pin_0, DHT1.VDD
  GND: Componente1.GND, DHT1.GND

notes:
  CIRCUITO 07
