# Fritzing sketch Codigo_08 (saved by Fritzing 0.9.3b)
breadboards: 1

parts:
  Componente1 = Arduino Uno (Rev3)
  J1 = Basic Servo

nets:
  N1: Componente1.D2, J1.pulse
  5V: Componente1.5V, J1.vcc
  GND: Componente1.GND, J1.gnd

notes:
  CIRCUITO 08
