# Fritzing sketch Codigo_09 (saved by Fritzing 0.9.3b)
breadboards: 1

parts:
  Componente1 = Arduino Uno (Rev3)
  J1 = Basic Servo
  R2 = Resistor [tolerance=±5% resistance=1k package=THT]
  R1 = Basic Flex Resistor  # not connected
  R3 = Basic Flex Resistor

nets:
  N1: Componente1.A0, R2.Pin_1, R3.pin_1
  N2: Componente1.D2, J1.pulse
  5V: Componente1.5V, J1.vcc, R2.Pin_0
  N3: Componente1.GND, R3.Pin_2

notes:
  CIRCUITO 09

custom parts:
  Basic Flex Resistor: A generic Flex resistor
