# Fritzing sketch Codigo_10 (saved by Fritzing 0.9.3b)
breadboards: 1

parts:
  Componente1 = Arduino Uno (Rev3)
  SparkFun1 = SoftPot Membrane Potentiometer - 50mm [part_number=SEN-08680]
  R2 = Resistor [tolerance=±5% resistance=1k package=THT]
  R3 = Resistor [tolerance=±5% resistance=330 package=THT]
  R4 = Resistor [tolerance=±5% resistance=330 package=THT]
  R5 = Resistor [tolerance=±5% resistance=330 package=THT]
  LED1 = RGB LED (com. cathode, rgb) [package="5 mm [THT]"]

nets:
  N1: Componente1.A0, SparkFun1.wiper, R2.Pin_0
  N2: Componente1.D2, R5.Pin_1
  N3: Componente1.D3_PWM, R4.Pin_1
  N4: Componente1.D4, R3.Pin_1
  N5: Componente1.5V, SparkFun1.leg2
  N6: Componente1.GND, SparkFun1.leg1, R2.Pin_1, LED1.green_anode
  N7: R3.Pin_0, LED1.red_anode
  N8: R4.Pin_0, LED1.common_cathode
  N9: R5.Pin_0, LED1.blue_anode

notes:
  CIRCUITO 10

custom parts:
  SoftPot Membrane Potentiometer - 50mm: These are very thin variable potentiometers. By pressing down on various parts of the strip, the resistance linearly changes from 100Ohms to 10,000Ohms allowing the user to very accurately calculate the relative position on the strip. Can be used as an accurate positional indicator for CNC head positioning, variable user input (volume level input for example), straight user input (multiple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
