# Fritzing sketch Codigo_11 (saved by Fritzing 0.9.3b)
breadboards: 1

parts:
  Componente1 = Arduino Uno (Rev3)
  R1 = TRIMPOT [package=trimpot_pth_s3_lock]
  U1 = LCD-16X2 [package=lcd-16x2_noholes]

nets:
  N1: Componente1.D11_PWM/MOSI, U1.DB0
  N2: Componente1.D12/MISO, U1.DB6
  N3: Componente1.D2, U1.VO
  N4: Componente1.D3_PWM, U1.RS
  N5: Componente1.D4, U1.R_W
  N6: Componente1.D5_PWM, U1.E
  5V: Componente1.5V, R1.CCW, U1.VDD, U1.A
  GND: Componente1.GND, R1.CW, U1.VSS, U1.DB5, U1.K
  N7: R1.WIPER, U1.DB7

notes:
  CIRCUITO 11
